# Fritzing sketch carrito (saved by Fritzing 0.8.7b)
breadboards: 1

parts:
  Parte1 = Arduino Uno (Rev3)
  M1 = DC Motor  # not connected
  M2 = DC Motor  # not connected
  IC1 = H-Bridge [package=THT]  # not connected
  VCC1 = Battery block 9V
  Parte2 = SRF05 Ultrasonic Rangefinder

nets:
  N1: Parte1.D12/MISO, Parte2.Trig
  N2: Parte1.D13/SCK, Parte2.Echo
  5V: Parte1.5V, Parte2.VCC
  GND: Parte1.GND, VCC1.-, Parte2.GND
