# Fritzing sketch estacionamiento (saved by Fritzing 0.8.7b)
breadboards: 1

parts:
  Parte1 = Arduino Uno (Rev3)
  J1 = Basic Servo
  7_Segment1 = 7 Segment Display
  S1 = Pushbutton [package="[THT]"]
  S2 = Pushbutton [package="[THT]"]
  R8 = 470 Ω Resistor [package=THT]
  R9 = 470 Ω Resistor [package=THT]  # not connected
  R10 = 470 Ω Resistor [package=THT]
  R11 = 470 Ω Resistor [package=THT]
  R12 = 470 Ω Resistor [package=THT]
  R13 = 470 Ω Resistor [package=THT]
  R14 = 470 Ω Resistor [package=THT]

nets:
  GND: Parte1.GND, J1.gnd, 7_Segment1.common_anode, S1.Pin_1, S1.Pin_2, S2.Pin_1, S2.Pin_2
  N1: Parte1.D10_PWM/SS, J1.pulse
  N2: Parte1.D11_PWM/MOSI, S1.Pin_3, S1.Pin_4
  N3: Parte1.D12/MISO, S2.Pin_3, S2.Pin_4
  N4: Parte1.D1/TX, R8.Pin_0
  N5: Parte1.D3_PWM, R10.Pin_0
  N6: Parte1.D4, R11.Pin_0
  N7: Parte1.D5_PWM, R12.Pin_0
  N8: Parte1.D6_PWM, R13.Pin_0
  N9: Parte1.D7, R14.Pin_0
  5V: Parte1.5V, J1.vcc
  N10: 7_Segment1.Segment_E, R12.Pin_1
  N11: 7_Segment1.Segment_D, R11.Pin_1
  N12: 7_Segment1.Segment_C, R10.Pin_1
  N13: 7_Segment1.Segment_A, R8.Pin_1
  N14: 7_Segment1.Segment_F, R13.Pin_1
  N15: 7_Segment1.Segment_G, R14.Pin_1

custom parts:
  470 Ω Resistor: A generic resistor (0.25W)
